# Fritzing sketch oha_101 (saved by Fritzing 0.7.11b)
breadboards: 1

parts:
  Arduino1 = Arduino
  R1 = Resistor [tolerance=±5% resistance=220 package=THT]
  LED1 = LED - 5mm [color="Red (633nm)" package="5 mm [THT]"]

nets:
  N1: Arduino1.D9, R1.Pin_1
  N2: Arduino1.GND, LED1.cathode
  N3: R1.Pin_0, LED1.anode
