# Fritzing sketch contact_sensor (saved by Fritzing 0.7.11b)
breadboards: 1

parts:
  Arduino1 = Arduino
  R1 = Resistor [tolerance=±5% resistance=220 package=THT]
  S1 = Pushbutton [package="[THT]"]

nets:
  N1: Arduino1.D2, R1.Pin_0, S1.Pin_1, S1.Pin_2
  N2: Arduino1.+5V, S1.Pin_3, S1.Pin_4
  N3: Arduino1.GND, R1.Pin_1
