# Fritzing sketch humidity_sensor (saved by Fritzing 0.7.11b)
breadboards: 1

parts:
  Arduino1 = Arduino
  DHT1 = DHT11 Humitidy and Temperature Sensor
  R1 = Resistor [tolerance=±5% resistance=10k package="0805 [SMD]"]  # not connected

nets:
  GND: Arduino1.GND, DHT1.GND
  N1: Arduino1.D2, DHT1.DATA
  +5V: Arduino1.+5V, DHT1.VDD

custom parts:
  DHT11 Humitidy and Temperature Sensor: DHT11 Humidity and Temperature Sensor
