# Fritzing sketch relay (saved by Fritzing 0.7.11b)
breadboards: 1

parts:
  Arduino1 = Arduino
  K1 = Relay [part_number=FRS1B-S package=THT]
  R1 = 470 Ω Resistor [package=THT]
  Q1 = NPN-Transistor [package="SOT-23 [SMD]"]
  R2 = 470 Ω Resistor [package=THT]
  LED1 = LED - 3mm [color="Red (633nm)" package="3 mm [THT]"]
  LED2 = LED - 3mm [color="Red (633nm)" package="3 mm [THT]"]
  D1 = Rectifier Diode [part_number=1N4001 package="Melf DO-213 AB [SMD]"]

nets (from the schematic view):
  N1: Arduino1.GND, Q1.2, LED1.cathode, LED2.cathode
  N2: Arduino1.D2, R1.Pin_1
  N3: Arduino1.+5V, K1.COIL1, R2.Pin_1, D1.cathode
  N4: K1.A, LED2.anode
  N5: K1.C1, K1.C2, R2.Pin_0
  N6: K1.COIL2, Q1.1, D1.anode
  N7: K1.B, LED1.anode
  N8: R1.Pin_0, Q1.0
