# Fritzing sketch dc_motor (saved by Fritzing 0.7.11b)
breadboards: 1

parts:
  Arduino1 = Arduino
  R1 = 470 Ω Resistor [package=THT]
  Q1 = NPN-Transistor [package="SOT-23 [SMD]"]
  D1 = Rectifier Diode [part_number=1N4001 package="Melf DO-213 AB [SMD]"]
  M1 = DC Motor

nets:
  N1: Arduino1.GND, Q1.2
  N2: Arduino1.D2, R1.Pin_0
  N3: Arduino1.+5V, D1.cathode, M1.pin_1
  N4: R1.Pin_1, Q1.0
  N5: Q1.1, D1.anode, M1.pin_2
