# Fritzing sketch dc_motor_ambient (saved by Fritzing 0.7.11b)
breadboards: 1

parts:
  Arduino1 = Arduino
  R2 = Resistor [tolerance=±5% resistance=220 package=THT]
  R3 = Photocell (LDR) [package=THT]
  IC1 = L293D [package=THT]
  M1 = DC Motor

nets:
  N1: Arduino1.GND, R2.Pin_0, IC1.0V
  N2: Arduino1.D6, IC1.Enable_1
  N3: Arduino1.D5, IC1.In_1
  N4: Arduino1.D4, IC1.In_2
  N5: Arduino1.+5V, R3.pin_1, IC1.+Vmotor, IC1.+V
  N6: Arduino1.A0, R2.Pin_1, R3.pin_0
  N7: IC1.Out_1_(_Controlled_by_Enable_1_), M1.pin_2
  N8: IC1.Out_2_(_Controlled_by_Enable_1_), M1.pin_1
