# Fritzing sketch motion_detector (saved by Fritzing 0.7.11b)
breadboards: 1

parts:
  Arduino1 = Arduino
  LED1 = LED - 3mm [color="Red (633nm)" package="3 mm [THT]"]
  R1 = 470 Ω Resistor [package=THT]
  PIR1 = PIR sensor

nets:
  N1: Arduino1.D7, PIR1.SIG
  N2: Arduino1.D2, R1.Pin_1
  +5V: Arduino1.+5V, PIR1.VDD
  GND: Arduino1.GND, LED1.cathode, PIR1.GND
  N3: LED1.anode, R1.Pin_0
