# Fritzing sketch light_levels (saved by Fritzing 0.7.11b)
breadboards: 1

parts:
  Arduino1 = Arduino
  LED1 = LED - 3mm [color="Red (633nm)" package="3 mm [THT]"]
  R1 = 470 Ω Resistor [package=THT]
  R2 = 470 Ω Resistor [package=THT]
  R3 = Photocell (LDR) [package=THT]

nets:
  N1: Arduino1.D2, R1.Pin_1
  N2: Arduino1.+5V, R3.pin_0
  N3: Arduino1.GND, LED1.cathode
  N4: Arduino1.A0, R2.Pin_0, R3.pin_1
  N5: LED1.anode, R1.Pin_0
