# Fritzing sketch rgb_led (saved by Fritzing 0.7.11b)
breadboards: 1

parts:
  Arduino1 = Arduino
  LED2 = RGB LED (com. cathode, rgb) [package="5 mm [THT]"]
  R1 = Resistor [tolerance=±5% resistance=470 package=THT]
  R2 = Resistor [tolerance=±5% resistance=470 package=THT]
  R3 = Resistor [tolerance=±5% resistance=470 package=THT]

nets:
  N1: Arduino1.D11, R3.Pin_1
  N2: Arduino1.D10, R2.Pin_1
  N3: Arduino1.D9, R1.Pin_1
  N4: Arduino1.+5V, LED2.common_cathode
  N5: LED2.red_anode, R1.Pin_0
  N6: LED2.green_anode, R2.Pin_0
  N7: LED2.blue_anode, R3.Pin_0
