# Fritzing sketch wifi_weather_station (saved by Fritzing 0.8.3b)

parts:
  DHT1 = DHT11 Humitidy and Temperature Sensor
  R2 = Resistor [tolerance=±5% resistance=10k package=THT]
  Part1 = Arduino Uno (Rev3)
  U1 = IC, DIP package, 10 pins [chip_label=CC3000]

nets:
  VDD: DHT1.VDD, R2.Pin_0, Part1.5V, U1.pin1
  N1: DHT1.DATA, Part1.D7
  GND: DHT1.GND, Part1.GND, U1.pin3
  N2: Part1.ICSP_MISO, Part1.D12/MISO, U1.pin5
  N3: Part1.ICSP_SCK, U1.pin4
  N4: Part1.ICSP_MOSI, Part1.D11_PWM/MOSI, U1.pin6
  N5: Part1.D10_PWM/SS, U1.pin7
  N6: Part1.D3_PWM, U1.pin9
  N7: Part1.D5_PWM, U1.pin8

custom parts:
  DHT11 Humitidy and Temperature Sensor: DHT11 Humidity and Temperature Sensor
